# Fritzing sketch analogRead() pin A0 (saved by Fritzing 0.9.3b)
breadboards: 1

parts:
  Componente1 = Arduino Uno (Rev3)
  R1 = Trimmer Potentiometer [maximum_resistance=10kΩ package=THT]

nets:
  N1: Componente1.A0, R1.wiper
  N2: Componente1.5V, R1.leg1
  N3: Componente1.GND, R1.leg2
